# Fritzing sketch garage_door_sensor (saved by Fritzing 0.9.9b)
breadboards: 1

parts:
  Part1 = Triple Axis Accelerometer Breakout - ADXL345
  Part2 = Wake-On-Shake Board
  U2 = NodeMCU V1.0
  S2 = Toggle Switch [package=THT]
  J1 = Power Jack [package=power_jack_smd]
  VCC1 = Battery block 9V  # not connected
  LED1 = smd LED [color="Red (633nm)" package="1206 [SMD]"]
  LED2 = smd LED [color="Green (555nm)" package="1206 [SMD]"]
  R1 = Resistor [tolerance=±5% power=0.25 resistance=220 package=THT]
  LED3 = smd LED [color="Yellow (585nm)" package="1206 [SMD]"]
  R2 = Resistor [tolerance=±5% power=0.25 resistance=220 package=THT]
  R3 = Resistor [tolerance=±5% power=0.25 resistance=220 package=THT]

nets:
  GND: Part1.GND, Part2.GND#30, U2.GND, R1.Pin_1, R2.Pin_1, R3.Pin_1
  VCC: Part1.VCC, U2.3V3
  N1: Part1.SDA, U2.D2
  N2: Part1.SCL, U2.D1
  N3: Part2.VIN, S2.L2
  N4: Part2.GND#22, J1.GND
  N5: Part2.WAKE, U2.SD3
  N6: Part2.VOUT, U2.Vin
  N7: U2.D6, LED1.anode
  N8: U2.D7, LED3.anode
  N9: U2.D8, LED2.anode
  N10: S2.COM, J1.GNDBREAK
  N11: LED1.cathode, R3.Pin_0
  N12: LED2.cathode, R1.Pin_0
  N13: LED3.cathode, R2.Pin_0

custom parts:
  Wake-On-Shake Board: Description: Have you ever wanted your project to just "hibernate" until someone picks it up or moves it? It's a great strategy for dramatically extending the battery life of a widget that doesn't need to be active all the time. The Wake-on-Shake board is designed to make it really simple to do just that! The Wake-on-Shake, based on a concept by Nitzan Gadish of Analog Devices, combines the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
  NodeMCU V1.0: ESP8266 based NodeMCU
